# Fritzing sketch PCB_compactadora (saved by Fritzing 0.9.3b)
circuit board: 15cm x 11cm
breadboards: 1

parts:
  V1A = DC Power [voltage=5V]
  RelevadorRLED = IC, DIP package, 6 pins [chip_label=IC]
  RelevadorGLED = IC, DIP package, 6 pins [chip_label=IC]
  RelevadorL = IC, DIP package, 6 pins [chip_label=IC]
  RelevadorR = IC, DIP package, 6 pins [chip_label=IC]
  V4 = DC Power [voltage=24V]
  V3 = DC Power [voltage=12V]
  V2 = DC Power [voltage=12V]
  V3_2 = DC Power [voltage=24V]
  Arduino_MEGA = Arduino Mega 2560 (Rev3)
  Load_Amp_1 = IC, SIP package, 5 pins [chip_label=HX711]
  Load_Amp_2 = IC, SIP package, 5 pins [chip_label=IC]  # not connected

nets:
  GND: V1A.V-, RelevadorRLED.pin2, RelevadorGLED.pin2, RelevadorL.pin2, RelevadorL.pin5, RelevadorR.pin2, RelevadorR.pin5, V3.V-, V2.V-, Arduino_MEGA.GND, Load_Amp_1.pin5
  N1: RelevadorRLED.pin1, RelevadorGLED.pin1, RelevadorL.pin1, RelevadorR.pin1, Arduino_MEGA.5V, Load_Amp_1.pin1, Load_Amp_1.pin2
  N2: RelevadorRLED.pin3, Arduino_MEGA.D46
  N3: RelevadorRLED.pin5, V2.V+
  N4: RelevadorGLED.pin3, Arduino_MEGA.D42
  N5: RelevadorGLED.pin5, V3.V+
  N6: RelevadorL.pin3, Arduino_MEGA.D28
  N7: RelevadorL.pin4, V3_2.V-
  N8: RelevadorR.pin3, Arduino_MEGA.D29
  N9: RelevadorR.pin4, V4.V-
  N10: Arduino_MEGA.D4_PWM, Load_Amp_1.pin3
  N11: Arduino_MEGA.D5_PWM, Load_Amp_1.pin4
